// Logisim project exampleLib.circ as structural Verilog: 3 circuits, main circuit simpleXor
module simpleXor (
  input  in0,
  input  in1,
  output out_3
);

  wire and_1_out, and_2_out, not_1_out, not_2_out;

  not not_1 (not_1_out, in0);
  not not_2 (not_2_out, in1);
  and and_1 (and_1_out, not_1_out, in1);
  and and_2 (and_2_out, in0, not_2_out);
  or or_1 (out_3, and_1_out, and_2_out);

  // Notes on the sheet:
  //   Circuito XOR - Arthur Lorencini Bergamaschi
endmodule

module Mux2x1 (
  input  in0,
  input  in1,
  input  selectPin,
  output out0
);

  wire and_1_out, and_2_out, not_1_out;

  not not_1 (not_1_out, selectPin);
  and and_1 (and_1_out, in0, not_1_out);
  and and_2 (and_2_out, in1, selectPin);
  or or_1 (out0, and_1_out, and_2_out);
endmodule

module Mux4x1 (
  input  in00,
  input  in01,
  input  in10,
  input  in11,
  input  select0,
  input  select1,
  output out0
);

  wire mux2x1_1_out0, mux2x1_2_out0;

  Mux2x1 mux2x1_1 (.selectPin(select1), .in0(in00), .in1(in01), .out0(mux2x1_1_out0));
  Mux2x1 mux2x1_2 (.selectPin(select1), .in0(in10), .in1(in11), .out0(mux2x1_2_out0));
  Mux2x1 mux2x1_3 (.selectPin(select0), .in0(mux2x1_1_out0), .in1(mux2x1_2_out0), .out0(out0));
endmodule
