// Logisim project aula1.circ as structural Verilog
module ALUcinado (
  input  [3:0] in_1
);

  wire [3:0] adder_1_out;

  Adder #(.width(4)) adder_1 (.a(in_1), .b(4'b0100), .out(adder_1_out));  // open: cin, cout
endmodule
