// Logisim project aula2.circ as structural Verilog
module registerBank32 (
);

  Register #(.width(32)) register_1 ();  // open: D, en, Q, clk, clr
  Register #(.width(32)) register_2 ();  // open: D, en, Q, clk, clr
  Register #(.width(32)) register_3 ();  // open: D, en, Q, clk, clr
  Register #(.width(32)) register_4 ();  // open: D, en, Q, clk, clr
  Register #(.width(32)) register_5 ();  // open: D, en, Q, clk, clr
  Register #(.width(32)) register_6 ();  // open: D, en, Q, clk, clr
  Register #(.width(32)) register_7 ();  // open: D, en, Q, clk, clr
  Register #(.width(32)) register_8 ();  // open: D, en, Q, clk, clr
  Register #(.width(32)) register_9 ();  // open: D, en, Q, clk, clr
  Register #(.width(32)) register_10 ();  // open: D, en, Q, clk, clr
  Register #(.width(32)) register_11 ();  // open: D, en, Q, clk, clr
  Register #(.width(32)) register_12 ();  // open: D, en, Q, clk, clr
  Register #(.width(32)) register_13 ();  // open: D, en, Q, clk, clr
  Register #(.width(32)) register_14 ();  // open: D, en, Q, clk, clr
  Register #(.width(32)) register_15 ();  // open: D, en, Q, clk, clr
  Register #(.width(32)) register_16 ();  // open: D, en, Q, clk, clr
  Register #(.width(32)) register_17 ();  // open: D, en, Q, clk, clr
  Register #(.width(32)) register_18 ();  // open: D, en, Q, clk, clr
  Register #(.width(32)) register_19 ();  // open: D, en, Q, clk, clr
  Register #(.width(32)) register_20 ();  // open: D, en, Q, clk, clr
  Register #(.width(32)) register_21 ();  // open: D, en, Q, clk, clr
  Register #(.width(32)) register_22 ();  // open: D, en, Q, clk, clr
  Register #(.width(32)) register_23 ();  // open: D, en, Q, clk, clr
  Register #(.width(32)) register_24 ();  // open: D, en, Q, clk, clr
  Register #(.width(32)) register_25 ();  // open: D, en, Q, clk, clr
  Register #(.width(32)) register_26 ();  // open: D, en, Q, clk, clr
  Register #(.width(32)) register_27 ();  // open: D, en, Q, clk, clr
  Register #(.width(32)) register_28 ();  // open: D, en, Q, clk, clr
  Register #(.width(32)) register_29 ();  // open: D, en, Q, clk, clr
  Register #(.width(32)) register_30 ();  // open: D, en, Q, clk, clr
  Register #(.width(32)) register_31 ();  // open: D, en, Q, clk, clr
  Register #(.width(32)) register_32 ();  // open: D, en, Q, clk, clr
endmodule
