// Logisim project forfun.circ as structural Verilog: 9 circuits, main circuit main
module main (
  input  in_1,
  input  in_2,
  output [31:0] out_3
);

  wire clock_1_out;
  wire [31:0] adder_1_out;

  Clock clock_1 (.out(clock_1_out));
  PC pc_1 (.in_in(adder_1_out), .w_enable(in_1), .clk(clock_1_out), .rst(in_2), .in_out(out_3));
  Adder #(.width(32)) adder_1 (.a(out_3), .b(32'h4), .out(adder_1_out));  // open: cin, cout

  // Notes on the sheet:
  //   Ctrl + T = Ativa o clock para simular
  //   Ctrl + K = Deixa simulando
endmodule

module register_bank (
  input  [4:0] in_1,
  input  [4:0] in_2,
  input  [4:0] w_reg,
  input  [31:0] w_data,
  input  w_enable,
  output [31:0] reg_out_1,
  output [31:0] reg_out_2
);

  wire clk_out;
  wire [7:0] demultiplexer_1_out0, demultiplexer_1_out8, demultiplexer_1_out16, demultiplexer_1_out24;
  wire [31:0] register_1_q, register_2_q, register_3_q, register_4_q, register_5_q, register_6_q,
       register_7_q, register_8_q, register_9_q, register_10_q, register_11_q, register_12_q, register_13_q,
       register_14_q, register_15_q, register_16_q, register_17_q, register_18_q, register_19_q,
       register_20_q, register_21_q, register_22_q, register_23_q, register_24_q, register_25_q,
       register_26_q, register_27_q, register_28_q, register_29_q, register_30_q, register_31_q,
       register_32_q;

  Clock clk (.out(clk_out));
  Demultiplexer #(.select(5), .enable("false")) demultiplexer_1 (
    .out0(demultiplexer_1_out0[0]), .out1(demultiplexer_1_out0[1]), .out2(demultiplexer_1_out0[2]),
    .out3(demultiplexer_1_out0[3]), .out4(demultiplexer_1_out0[4]), .out5(demultiplexer_1_out0[5]),
    .out6(demultiplexer_1_out0[6]), .out7(demultiplexer_1_out0[7]), .out8(demultiplexer_1_out8[0]),
    .out9(demultiplexer_1_out8[1]), .out10(demultiplexer_1_out8[2]), .out11(demultiplexer_1_out8[3]),
    .out12(demultiplexer_1_out8[4]), .out13(demultiplexer_1_out8[5]), .out14(demultiplexer_1_out8[6]),
    .out15(demultiplexer_1_out8[7]), .out16(demultiplexer_1_out16[0]), .out17(demultiplexer_1_out16[1]),
    .out18(demultiplexer_1_out16[2]), .out19(demultiplexer_1_out16[3]), .out20(demultiplexer_1_out16[4]),
    .out21(demultiplexer_1_out16[5]), .out22(demultiplexer_1_out16[6]), .out23(demultiplexer_1_out16[7]),
    .out24(demultiplexer_1_out24[0]), .out25(demultiplexer_1_out24[1]), .out26(demultiplexer_1_out24[2]),
    .out27(demultiplexer_1_out24[3]), .out28(demultiplexer_1_out24[4]), .out29(demultiplexer_1_out24[5]),
    .out30(demultiplexer_1_out24[6]), .out31(demultiplexer_1_out24[7]), .in(w_enable), .sel(w_reg));
  Register #(.width(32)) register_1 (
    .D(w_data), .en(demultiplexer_1_out0[0]), .clk(clk_out), .Q(register_1_q), .clr(1'b0));
  Register #(.width(32)) register_2 (
    .D(w_data), .en(demultiplexer_1_out0[1]), .clk(clk_out), .Q(register_2_q), .clr(1'b0));
  Register #(.width(32)) register_3 (
    .D(w_data), .en(demultiplexer_1_out0[2]), .clk(clk_out), .Q(register_3_q), .clr(1'b0));
  Register #(.width(32)) register_4 (
    .D(w_data), .en(demultiplexer_1_out0[3]), .clk(clk_out), .Q(register_4_q), .clr(1'b0));
  Register #(.width(32)) register_5 (
    .D(w_data), .en(demultiplexer_1_out0[4]), .clk(clk_out), .Q(register_5_q), .clr(1'b0));
  Register #(.width(32)) register_6 (
    .D(w_data), .en(demultiplexer_1_out0[5]), .clk(clk_out), .Q(register_6_q), .clr(1'b0));
  Register #(.width(32)) register_7 (
    .D(w_data), .en(demultiplexer_1_out0[6]), .clk(clk_out), .Q(register_7_q), .clr(1'b0));
  Register #(.width(32)) register_8 (
    .D(w_data), .en(demultiplexer_1_out0[7]), .clk(clk_out), .Q(register_8_q), .clr(1'b0));
  Register #(.width(32)) register_9 (
    .D(w_data), .en(demultiplexer_1_out8[0]), .clk(clk_out), .Q(register_9_q), .clr(1'b0));
  Register #(.width(32)) register_10 (
    .D(w_data), .en(demultiplexer_1_out8[1]), .clk(clk_out), .Q(register_10_q), .clr(1'b0));
  Register #(.width(32)) register_11 (
    .D(w_data), .en(demultiplexer_1_out8[2]), .clk(clk_out), .Q(register_11_q), .clr(1'b0));
  Register #(.width(32)) register_12 (
    .D(w_data), .en(demultiplexer_1_out8[3]), .clk(clk_out), .Q(register_12_q), .clr(1'b0));
  Register #(.width(32)) register_13 (
    .D(w_data), .en(demultiplexer_1_out8[4]), .clk(clk_out), .Q(register_13_q), .clr(1'b0));
  Register #(.width(32)) register_14 (
    .D(w_data), .en(demultiplexer_1_out8[5]), .clk(clk_out), .Q(register_14_q), .clr(1'b0));
  Register #(.width(32)) register_15 (
    .D(w_data), .en(demultiplexer_1_out8[6]), .clk(clk_out), .Q(register_15_q), .clr(1'b0));
  Register #(.width(32)) register_16 (
    .D(w_data), .en(demultiplexer_1_out8[7]), .clk(clk_out), .Q(register_16_q), .clr(1'b0));
  Register #(.width(32)) register_17 (
    .D(w_data), .en(demultiplexer_1_out16[0]), .clk(clk_out), .Q(register_17_q), .clr(1'b0));
  Register #(.width(32)) register_18 (
    .D(w_data), .en(demultiplexer_1_out16[1]), .clk(clk_out), .Q(register_18_q), .clr(1'b0));
  Register #(.width(32)) register_19 (
    .D(w_data), .en(demultiplexer_1_out16[2]), .clk(clk_out), .Q(register_19_q), .clr(1'b0));
  Register #(.width(32)) register_20 (
    .D(w_data), .en(demultiplexer_1_out16[3]), .clk(clk_out), .Q(register_20_q), .clr(1'b0));
  Register #(.width(32)) register_21 (
    .D(w_data), .en(demultiplexer_1_out16[4]), .clk(clk_out), .Q(register_21_q), .clr(1'b0));
  Register #(.width(32)) register_22 (
    .D(w_data), .en(demultiplexer_1_out16[5]), .clk(clk_out), .Q(register_22_q), .clr(1'b0));
  Register #(.width(32)) register_23 (
    .D(w_data), .en(demultiplexer_1_out16[6]), .clk(clk_out), .Q(register_23_q), .clr(1'b0));
  Register #(.width(32)) register_24 (
    .D(w_data), .en(demultiplexer_1_out16[7]), .clk(clk_out), .Q(register_24_q), .clr(1'b0));
  Register #(.width(32)) register_25 (
    .D(w_data), .en(demultiplexer_1_out24[0]), .clk(clk_out), .Q(register_25_q), .clr(1'b0));
  Register #(.width(32)) register_26 (
    .D(w_data), .en(demultiplexer_1_out24[1]), .clk(clk_out), .Q(register_26_q), .clr(1'b0));
  Register #(.width(32)) register_27 (
    .D(w_data), .en(demultiplexer_1_out24[2]), .clk(clk_out), .Q(register_27_q), .clr(1'b0));
  Register #(.width(32)) register_28 (
    .D(w_data), .en(demultiplexer_1_out24[3]), .clk(clk_out), .Q(register_28_q), .clr(1'b0));
  Register #(.width(32)) register_29 (
    .D(w_data), .en(demultiplexer_1_out24[4]), .clk(clk_out), .Q(register_29_q), .clr(1'b0));
  Register #(.width(32)) register_30 (
    .D(w_data), .en(demultiplexer_1_out24[5]), .clk(clk_out), .Q(register_30_q), .clr(1'b0));
  Register #(.width(32)) register_31 (
    .D(w_data), .en(demultiplexer_1_out24[6]), .clk(clk_out), .Q(register_31_q), .clr(1'b0));
  Register #(.width(32)) register_32 (
    .D(w_data), .en(demultiplexer_1_out24[7]), .clk(clk_out), .Q(register_32_q), .clr(1'b0));
  Multiplexer #(.select(5), .width(32), .enable("false")) multiplexer_1 (
    .in0(register_1_q), .in1(register_2_q), .in2(register_3_q), .in3(register_4_q), .in4(register_5_q),
    .in5(register_6_q), .in6(register_7_q), .in7(register_8_q), .in8(register_9_q), .in9(register_10_q),
    .in10(register_11_q), .in11(register_12_q), .in12(register_13_q), .in13(register_14_q),
    .in14(register_15_q), .in15(register_16_q), .in16(register_17_q), .in17(register_18_q),
    .in18(register_19_q), .in19(register_20_q), .in20(register_21_q), .in21(register_22_q),
    .in22(register_23_q), .in23(register_24_q), .in24(register_25_q), .in25(register_26_q),
    .in26(register_27_q), .in27(register_28_q), .in28(register_29_q), .in29(register_30_q),
    .in30(register_31_q), .in31(register_32_q), .out(reg_out_1), .sel(in_1));
  Multiplexer #(.select(5), .width(32), .enable("false")) multiplexer_2 (
    .in0(register_1_q), .in1(register_2_q), .in2(register_3_q), .in3(register_4_q), .in4(register_5_q),
    .in5(register_6_q), .in6(register_7_q), .in7(register_8_q), .in8(register_9_q), .in9(register_10_q),
    .in10(register_11_q), .in11(register_12_q), .in12(register_13_q), .in13(register_14_q),
    .in14(register_15_q), .in15(register_16_q), .in16(register_17_q), .in17(register_18_q),
    .in18(register_19_q), .in19(register_20_q), .in20(register_21_q), .in21(register_22_q),
    .in22(register_23_q), .in23(register_24_q), .in24(register_25_q), .in25(register_26_q),
    .in26(register_27_q), .in27(register_28_q), .in28(register_29_q), .in29(register_30_q),
    .in30(register_31_q), .in31(register_32_q), .out(reg_out_2), .sel(in_2));

  // Notes on the sheet:
  //   valor a ser gravado em w_reg
  //   aqui entram os enderecos a serem lidos/escritos
  //   Qual registrador voce quer gravar o valor de w_data
  //   0-31
  //   clk eh ligado no clk de todos os registradores
  //   w_enable habilita ou nao a escrita
  //   w_reg controla o dmx
  //   8-15
  //   24-32
  //   0-7
  //   16-23
  //   regs de 0-7
  //   regs de 8 - 15
  //   regs de 16 - 23
  //   regs de 24 - 32
  //   aqui sai o valor armazenado no primeiro endereco
  //   aqui sai o segundo valor dado pelo endereco
endmodule

module fetch (
  input  Enable,
  input  Reset,
  output [31:0] instruction
);

  wire clk_out;
  wire [31:0] program_counter_q;

  Register #(.width(32)) program_counter (
    .D(instruction), .en(Enable), .clk(clk_out), .Q(program_counter_q), .clr(Reset));
  Clock clk (.out(clk_out));
  Adder #(.width(32)) adder_1 (.a(program_counter_q), .b(32'h4), .out(instruction));  // open: cin, cout

  // Notes on the sheet:
  //   fetch = buscar/trazer
  //   Exemplo de circuito responsavel por incrementar PC em 4
  //   Serve para seguir com as próximas instrucoes na memoria
  //   nao precisaremos colocar na main. eh so um exemplo
endmodule

module PC (
  input  [31:0] in_in,
  input  w_enable,
  input  clk,
  input  rst,
  output [31:0] in_out
);

  Register #(.width(32)) program_counter (.D(in_in), .en(w_enable), .clk(clk), .Q(in_out), .clr(rst));

  // Notes on the sheet:
  //   PC = Program Counter = Contador de Programas. Responsavel por armazenar o valor de entrada e jogar no incrementador
  //   Ele armazena o endereco da instrucao e joga para instruction_memory. Depois eh incrementado em 4 por causa da memoria
endmodule

module instruction_memory (
  input  [31:0] read_adress,
  output [31:0] instruction
);

  ROM #(.addrWidth(24), .dataWidth(32)) rom_1 (.addr(read_adress[25:2]), .data(instruction));

  // Notes on the sheet:
  //   32bit
  //   only multiple
  //   of 4
  //   26 - 31 nao importam
  //   Exemplo: entra 0xc
  //   0 e 1 sao o "offset bit"
  //   24bit
  //   the memory is accessed by interval of 4 and 4. So you dont need the first 2 wires
  //   Essa daqui eh onde as instrucoes ficam armazenadas
  //   2 to the power of 24 is 16777215
  //   endereco - instrucao
  //   quem chama essas instrucoes eh o Program Counter (PC) usando um endereco de 32bit
  //   32bit
  //   Sai o terceiro valor pois c = 12 = 4 x 3 
  //   Pressupoe-se que as instrucoes ja estejam previamente salvas
  //   Usa-se memoria ROM, ou seja, ela so pode ser lida. (Read Only Memory),
endmodule

module ALU (
  input  [31:0] alu_in_1,
  input  [31:0] alu_in_2,
  input  [3:0] alu_op
);

  wire [31:0] adder_1_out, and_1_out, nor_1_out, or_1_out, subtractor_1_out;

  Adder #(.width(32)) adder_1 (.a(alu_in_1), .b(alu_in_2), .out(adder_1_out));  // open: cin, cout
  Subtractor #(.width(32)) subtractor_1 (.a(alu_in_1), .b(alu_in_2), .out(subtractor_1_out));  // open: bin, bout
  assign and_1_out = alu_in_1 & alu_in_2;  // AND_Gate and_1, 32 bits wide
  assign or_1_out = alu_in_1 | alu_in_2;  // OR_Gate or_1, 32 bits wide
  assign nor_1_out = ~(alu_in_1 | alu_in_2);  // NOR_Gate nor_1, 32 bits wide
  Multiplexer #(.select(4), .width(32), .enable("false")) multiplexer_1 (.sel(alu_op));  // open: in0, in1, in2, in3, in4, in5, in6, in7, in8, in9, in10, in11, in12, in13, in14, in15, out

  // Notes on the sheet:
  //   fios separados do segundo reg
endmodule

module sign_extend (
  input  [15:0] in_addr,
  output [31:0] out_addr
);


  assign out_addr = {{17{in_addr[15]}}, in_addr[14:0]};

  // Notes on the sheet:
  //   16 bit
  //   O extensor de sinal (signal extensor) pega o valor do campo address da instrucao e extende ele
  //   32 bit
  //   o bit 15 eh copiado para os bit de 16 a 31. Ao fazer isso, preserva-se o valor em complemento de 2
  //   exemplo simples: 1011 = -5 (4bits) -> 11011 = -5 (agora com 5 bits)
endmodule

module data_memory (
  input  [31:0] rw_address,
  input  [31:0] w_data,
  input  mem_write,
  input  [1:0] whb,
  output [31:0] r_data
);

  wire undriven;
  wire [1:0] demultiplexer_1_out0, demultiplexer_1_out1;
  wire [3:0] demultiplexer_2_out0, multiplexer_2_out;
  wire [7:0] demultiplexer_4_out0, demultiplexer_4_out1, demultiplexer_4_out2, demultiplexer_4_out3,
       multiplexer_3_out, ram_3_dout, ram_4_dout;
  wire [15:0] demultiplexer_3_out0, demultiplexer_3_out1, multiplexer_4_out, ram_1_dout;
  wire [31:0] multiplexer_1_out;

  Demultiplexer #(.width(2), .enable("false")) demultiplexer_1 (
    .out0(demultiplexer_1_out0), .out1(demultiplexer_1_out1), .in({2{mem_write}}), .sel(rw_address[1]));
  Demultiplexer #(.select(2), .enable("false")) demultiplexer_2 (
    .out0(demultiplexer_2_out0[0]), .out1(demultiplexer_2_out0[1]), .out2(demultiplexer_2_out0[2]),
    .out3(demultiplexer_2_out0[3]), .in(mem_write), .sel(rw_address[1:0]));
  Demultiplexer #(.width(16), .enable("false")) demultiplexer_3 (
    .out0(demultiplexer_3_out0), .out1(demultiplexer_3_out1), .in(w_data[15:0]), .sel(rw_address[1]));
  Demultiplexer #(.select(2), .width(8), .enable("false")) demultiplexer_4 (
    .out0(demultiplexer_4_out0), .out1(demultiplexer_4_out1), .out2(demultiplexer_4_out2),
    .out3(demultiplexer_4_out3), .in(w_data[7:0]), .sel(rw_address[1:0]));
  Multiplexer #(.select(2), .width(32), .enable("false")) multiplexer_1 (
    .in0(w_data), .in1({demultiplexer_3_out1, demultiplexer_3_out0}),
    .in2({demultiplexer_4_out3, demultiplexer_4_out2, demultiplexer_4_out1, demultiplexer_4_out0}),
    .out(multiplexer_1_out), .sel(whb));  // open: in3
  Multiplexer #(.select(2), .width(4), .enable("false")) multiplexer_2 (
    .in0({4{mem_write}}), .in1({demultiplexer_1_out1, demultiplexer_1_out0}), .in2(demultiplexer_2_out0),
    .out(multiplexer_2_out), .sel(whb));  // open: in3
  RAM #(.addrWidth(24), .trigger("high"), .databus("bibus")) ram_1 (
    .addr(rw_address[25:2]), .we(multiplexer_2_out[0]), .oe(undriven), .din(multiplexer_1_out[7:0]),
    .dout(ram_1_dout[7:0]));
  RAM #(.addrWidth(24), .trigger("high"), .databus("bibus")) ram_2 (
    .addr(rw_address[25:2]), .we(multiplexer_2_out[1]), .oe(undriven), .din(multiplexer_1_out[15:8]),
    .dout(ram_1_dout[15:8]));
  RAM #(.addrWidth(24), .trigger("high"), .databus("bibus")) ram_3 (
    .addr(rw_address[25:2]), .we(multiplexer_2_out[2]), .oe(undriven), .din(multiplexer_1_out[23:16]),
    .dout(ram_3_dout));
  RAM #(.addrWidth(24), .trigger("high"), .databus("bibus")) ram_4 (
    .addr(rw_address[25:2]), .we(multiplexer_2_out[3]), .oe(undriven), .din(multiplexer_1_out[31:24]),
    .dout(ram_4_dout));
  Multiplexer #(.select(2), .width(8), .enable("false")) multiplexer_3 (
    .in0(ram_1_dout[7:0]), .in1(ram_1_dout[15:8]), .in2(ram_3_dout), .in3(ram_4_dout),
    .out(multiplexer_3_out), .sel(rw_address[1:0]));
  Multiplexer #(.width(16), .enable("false")) multiplexer_4 (
    .in0(ram_1_dout), .in1({ram_4_dout, ram_3_dout}), .out(multiplexer_4_out), .sel(rw_address[1]));
  Multiplexer #(.select(2), .width(32), .enable("false")) multiplexer_5 (
    .in0({ram_4_dout, ram_3_dout, ram_1_dout}), .in1({{16{1'b0}}, multiplexer_4_out}),
    .in2({{24{1'b0}}, multiplexer_3_out}), .out(r_data), .sel(whb));  // open: in3

  // Notes on the sheet:
  //   permite escrever
  //   whb = write history bits (??)
  //   endereco a ser gravado
  //   valor a ser gravado no endereco acima
  //   Lembre-se que a memoria da MIPS eh acessada de 4 em 4
  //   Nao consigo entender internamente o seu funcionamento
  //   nao entendo ainda pra onde vai esses dois fios
  //   sinal de controle (?)
  //   Essa eh a memoria de dados, Aqui ficam armazenado os valores que voce vai escrevendo.
  //   Acesse usando um endereco, leia ou escreva no endereco desejado
  //   saida dos write enables
  //   endereco
  //   8 enderecos de 32bits para guardar um valor de 32bits
  //   Endereco - valor
  //   valor armazenado no endereco fornecido
endmodule

module shift_r_2 (
  input  [31:0] in_1,
  output [31:0] out_2
);


  assign out_2 = {in_1[29:0], 2'b00};

  // Notes on the sheet:
  //   pular para a instrucao PC + 4 + (valor no campo address da instrucao)*4
  //   Eh parte do circuito de Branch -> if e else
  //   O motivo pra dar esse shitf, se eu n to doido, eh para se a logica der verdadeira
  //   shift right 2 
  //   Esse circuito poe 2 zeros nos bits 0 e 1 da entrada. Faz tudo multiplicar por 4
  //   foda-se os ultimos 2
endmodule
